# Fritzing sketch buzzer_wiring (saved by Fritzing 0.9.3b)
breadboards: 1

parts:
  J1 = Piezo Speaker
  Raspberry_Pi1 = Raspberry Pi B+
  S1 = Pushbutton [package="[SMD]"]

nets:
  N1: J1.pin1, Raspberry_Pi1.GND, S1.Pin_3, S1.Pin_4
  N2: J1.pin2, Raspberry_Pi1.GPIO26
  N3: Raspberry_Pi1.GPIO21, S1.Pin_1, S1.Pin_2
